# Fritzing sketch schematic (saved by Fritzing 0.9.10b)

parts:
  Pico_H1 = Raspberry Pi Pico H  # not connected
  LED1 = RGB LED (com. cathode, rgb) [package="5 mm [THT]"]
  S1 = Pushbutton [package="[SMD]"]
  Mod1 = Raspberry Pi Pico

nets:
  N1: LED1.red_anode, Mod1.pin_15
  N2: LED1.common_cathode, S1.Pin_1, S1.Pin_2, Mod1.pin_18, Mod1.pin_23, Mod1.pin_33
  N3: LED1.green_anode, Mod1.pin_17
  N4: LED1.blue_anode, Mod1.pin_16
  N5: S1.Pin_3, S1.Pin_4, Mod1.pin_22

custom parts:
  Raspberry Pi Pico H: Raspberry Pi Pico H. Based around the RP2040 microcontroller the Pico H is a low cost microcontroller device bringing Raspberry Pi quality, cost, and easy of use to the microcontroller space.
  Raspberry Pi Pico: Raspberry Pi Pico. Based around the RP2040 microcontroller the Pico is a low cost microcontroller device bringing Raspberry Pi quality, cost, and easy of use to the microcontroller space. Jan 2021, Split part in to two versions: tht (this one) and SMD. This one will drill holes for a .1 in header in pcb to allow plugging in the module as well as providing pads to solder the module to the top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
